// Logisim project 2-4-decoder.circ as structural Verilog: 1 circuit, main circuit main
module main (
  input  A1,
  input  A0,
  output out_3,
  output out_4,
  output out_5,
  output out_6
);

  wire not_1_out, not_2_out;

  not not_1 (not_1_out, A1);
  not not_2 (not_2_out, A0);
  and Y0 (out_3, not_2_out, not_1_out);
  and Y1 (out_4, A0, not_1_out, not_1_out);
  and Y2 (out_5, A1, not_2_out);
  and Y3 (out_6, A1, A0);
endmodule
