// Logisim project d-flipflop.circ as structural Verilog: 3 circuits, main circuit main
module main (
  input  [3:0] Z
);

  Clock clock_1 ();  // open: out
  d_flipflop d_flipflop_1 ();  // open: in_2, in_1, out_3
endmodule

module d_latch (
  input  CLK,
  input  D,
  output Q,
  output Q_prime
);

  wire and_1_out, and_2_out, not_1_out;

  not not_1 (not_1_out, D);
  and and_1 (and_1_out, CLK, not_1_out);
  and and_2 (and_2_out, CLK, D);
  nor nor_1 (Q, and_1_out, Q_prime);
  nor nor_2 (Q_prime, Q, and_2_out);
endmodule

module d_flipflop (
  input  in_1,
  input  in_2,
  output out_3
);

  wire L1_q, not_1_out;

  not not_1 (not_1_out, in_1);
  d_latch L1 (.CLK(not_1_out), .D(in_2), .Q(L1_q));  // open: Q_prime
  d_latch L2 (.CLK(in_1), .D(L1_q), .Q(out_3));  // open: Q_prime
endmodule
