// Logisim project d-latch.circ as structural Verilog: 2 circuits, main circuit main
module main (
  input  D,
  output Q,
  output Q_prime
);

  wire and_1_out, and_2_out, CLK_out, not_1_out;

  Clock CLK (.out(CLK_out));
  not not_1 (not_1_out, D);
  and and_1 (and_1_out, CLK_out, not_1_out);
  and and_2 (and_2_out, CLK_out, D);
  nor nor_1 (Q, and_1_out, Q_prime);
  nor nor_2 (Q_prime, Q, and_2_out);
endmodule

module d_latch (
  input  D,
  output Q,
  output Q_prime
);

  wire and_1_out, and_2_out, CLK_out, not_1_out;

  Clock CLK (.out(CLK_out));
  not not_1 (not_1_out, D);
  and and_1 (and_1_out, CLK_out, not_1_out);
  and and_2 (and_2_out, CLK_out, D);
  nor nor_1 (Q, and_1_out, Q_prime);
  nor nor_2 (Q_prime, Q, and_2_out);
endmodule
