// Logisim project task21.circ as structural Verilog: 1 circuit, main circuit main
module main (
  input  D0,
  input  in_2,
  input  [1:0] in_3,
  input  D1,
  input  D2,
  input  D3,
  output MUX_Out,
  output Equal
);

  wire multiplexer_2_out, multiplexer_3_out, multiplexer_4_out;

  Multiplexer #(.select(2)) multiplexer_1 (
    .in0(D0), .in1(D1), .in2(D2), .in3(D3), .out(MUX_Out), .sel(in_3), .en(in_2));
  Multiplexer #(.enable("false")) multiplexer_2 (.in0(D0), .in1(D1), .out(multiplexer_2_out), .sel(in_3[0]));
  Multiplexer #(.enable("false")) multiplexer_3 (.in0(D2), .in1(D3), .out(multiplexer_3_out), .sel(in_3[0]));
  Multiplexer #(.enable("false")) multiplexer_4 (
    .in0(multiplexer_2_out), .in1(multiplexer_3_out), .out(multiplexer_4_out), .sel(in_3[1]));
  xor xor_1 (Equal, MUX_Out, multiplexer_4_out);
endmodule
